# Fritzing sketch Projeto esquema (saved by Fritzing 0.9.4)
breadboards: 1

parts:
  2_Channel_Relay1 = 2 Channel Power Relay
  Componente1 = Arduino Uno (Rev3) - ICSP
  부품3 = FC-28 Soil Hygrometer Module - Probe
  부품4 = FC-28 Soil Hygrometer Module
  M1 = DC Motor

nets:
  N1: 2_Channel_Relay1.JD-VCC, 2_Channel_Relay1.VCC#9
  GND: 2_Channel_Relay1.GND, Componente1.GND, 부품4.GND, M1.pin_1
  N2: 2_Channel_Relay1.IN1, Componente1.D8
  5V: 2_Channel_Relay1.VCC#14, 2_Channel_Relay1.K1-NO, Componente1.5V, 부품4.VCC
  N3: 2_Channel_Relay1.K1-COM, M1.pin_2
  N4: Componente1.A0, 부품4.AO
  N5: 부품3.POS, 부품4.POS
  N6: 부품3.NEG, 부품4.NEG

custom parts:
  2 Channel Power Relay: A 2 channel power relay. The module operates at 5V.
  FC-28 Soil Hygrometer Module - Probe: The FC-28 is a soil hygrometer module that uses the Texas Instruments LM393 comparator chip to provide an analog measurement of soil humidity.
  FC-28 Soil Hygrometer Module: The FC-28 is a soil hygrometer module that uses the Texas Instruments LM393 comparator chip to provide an analog measurement of soil humidity. The digital output is high when soil moisture is over a certain threshold, as determined by adjusting the potentiometer.
